# Fritzing sketch IR (saved by Fritzing 0.9.3b)

parts:
  IR1 = TSOP312.., 314.. [package=THT]
  Part1 = Arduino Uno (Rev3)

nets:
  N1: IR1.GND, Part1.D11_PWM/MOSI
  N2: IR1.Vs, Part1.GND
  N3: IR1.Data, Part1.5V

// code stored in the sketch: Untitled.ino
/*
* iRremote: IRecvDemo - demonstes receiving IR codes with IRrecv
* An IR dector /demodulator must be connected to the input RECV_PIN.
* Version 0.1 july, 2009
* Copyright 2009 Ken shirriff
* http://arcfn.com
*/

#include <IRremote.h>

int RECV_PIN = 11;

IRrecv irrecv(RECV_PIN);

decode_results results;

void setup()
{
Serial.begin(9600);
irrecv.enableIRIN(); //Start the reciver
}

void loop(){
if (irrecv.decode(&results)){
  Seerial.println(results.value, HEX);
  IRRECV.resume(); //Recive the next value
  }
  delay(100); 
  }
//LED1-ON
//LED1-OFF
//LED2-ON
//LED2-OFF
//LED3-ON
//LED3-OFF
